# Fritzing sketch EstacionMBalunC2026Circuito (saved by Fritzing 1.0.5)
circuit board: 8.46667cm x 5.64444cm
breadboards: 1

parts:
  Componente1 = Arduino Uno (Rev3)
  M1 = DC Motor [voltage_(max)=6V voltage_(min)=3V]
  DHT1 = Humidity and Temperature Sensor DHT11
  DHT2 = Humidity and Temperature Sensor DHT11
  M2 = BME280
  R2 = Resistor [tolerance=±5% power=0.25W resistance=220 package=THT]
  R3 = Resistor [tolerance=±5% power=0.25W resistance=220 package=THT]
  R4 = Resistor [tolerance=±5% power=0.25W resistance=220 package=THT]
  R5 = Resistor [tolerance=±5% power=0.25W resistance=220 package=THT]
  Sensor1 = Gas Sensor Breakout Board
  S1 = Reed switch [package=THT]
  R6 = Resistor [tolerance=±5% power=0.25W resistance=220 package=THT]

nets (from the breadboard view):
  N1: Componente1.A1, Sensor1.AOUT
  N2: Componente1.A3, M1.pin_2
  N3: Componente1.A4/SDA, M2.SDA, R2.Pin_1
  N4: Componente1.A5/SCL, M2.SCL, R3.Pin_1
  N5: Componente1.D8, DHT1.Data-signal, R4.Pin_1
  N6: Componente1.D3_PWM, S1.pin_1, R6.Pin_1
  N7: Componente1.D4, DHT1.Vcc
  N8: Componente1.D5_PWM, DHT2.Data-signal, R5.Pin_1
  N9: Componente1.D7, DHT2.Vcc
  3V3: Componente1.3V3, M2.VIN, R2.Pin_0, R3.Pin_0, R4.Pin_0, R5.Pin_0, R6.Pin_0
  5V: Componente1.5V, Sensor1.5V
  GND: Componente1.GND, M1.pin_1, DHT1.GND_2, DHT2.GND_2, M2.GND, Sensor1.GND, S1.pin_2

custom parts:
  Humidity and Temperature Sensor DHT11: Digital relative humidity & temperature sensor DHT11
  BME280: Temperature Humidity Barometric presure Sensor
  Gas Sensor Breakout Board: Gas sensor breakout board. Input voltage is 5V. Sensor output is available in analog and digital.

// code stored in the sketch: Untitled2.ino
#include <SofwareSerial.ht>

#include <Adafruit_BMP280.h>
#include <Adafruit_Sensor.h>
#include <Wire.h>
#include <DHT.h>
#include <DHT_U.h>




Adafruit_BMP280 bmp;

  #define DHTPIN1 2
  #define DHTPIN2 7
  #define DHTTYPE DHT11

DHT dht1(DHTPIN1,DHTTYPE);
DHT dht2(DHTPIN2,DHTTYPE); //solo para pruebas

  float temp;
  float pres;


void setup() {
 Serial.begin(9600);
 dht1.begin();
 dht2.begin(); //SOMBRA
 Wire.begin();
 bmp.begin(0x76);
}

void loop() {
  float tem1 = dht1.readTemperature();
  float hum1 = dht1.readHumidity();
  float tem2 = dht2.readTemperature(); //SOMBRA
 temp = bmp.readTemperature();
 pres = bmp.readPressure()/100;

  Serial.print("temperatura actual: ");
  Serial.print(temp);
  Serial.print("C*");
  Serial.print("pression atmosferica: ");
  Serial.print(pres);
  Serial.print("hpa");


  Serial.print("temperatura actual exterior: ");
  Serial.print(tem1);
  Serial.print("C* ");
  Serial.print("temperatura actual sombra: "); // Unicamente para pruebas.
  Serial.print(tem2);
  Serial.print("C* ");
  Serial.print(" humedad relativa: ");
  Serial.print(hum1);
  Serial.print("% ");

 delay(4000);
}
